# Fritzing sketch Botao (saved by Fritzing 0.9.3b)
breadboards: 1

parts:
  Part1 = Arduino Uno (Rev3)
  S2 = Pushbutton [package="[SMD]"]

nets:
  N1: Part1.D8, S2.Pin_3, S2.Pin_4
  N2: Part1.GND, S2.Pin_1, S2.Pin_2
