# Fritzing sketch Controlador-MIDI-teste (saved by Fritzing 0.9.3b)
breadboards: 1

parts:
  Part1 = Arduino Uno (Rev3)
  R1 = Rotary Potentiometer (Small) [maximum_resistance=100kΩ package=THT]
  S1 = Pushbutton [package="[THT]"]
  S2 = Pushbutton [package="[THT]"]

nets:
  N1: Part1.A0, R1.wiper
  N2: Part1.D8, S1.Pin_3, S1.Pin_4
  N3: Part1.D9_PWM, S2.Pin_3, S2.Pin_4
  N4: Part1.5V, R1.leg2
  N5: Part1.GND, R1.leg1, S1.Pin_1, S1.Pin_2, S2.Pin_1, S2.Pin_2
