# Fritzing sketch miniMIDIctrl (saved by Fritzing 0.9.3b)

parts:
  Part1 = Arduino Uno (Rev3)
  S2 = Pushbutton [package="[SMD]"]
  S3 = Pushbutton [package="[SMD]"]
  S4 = Pushbutton [package="[SMD]"]
  S5 = Pushbutton [package="[SMD]"]
  S6 = Pushbutton [package="[SMD]"]
  S7 = Pushbutton [package="[SMD]"]
  S8 = Pushbutton [package="[SMD]"]
  S9 = Pushbutton [package="[SMD]"]
  S10 = Pushbutton [package="[SMD]"]
  S11 = Pushbutton [package="[SMD]"]
  S12 = Pushbutton [package="[SMD]"]
  S13 = Pushbutton [package="[SMD]"]
  S14 = Pushbutton [package="[SMD]"]
  S15 = Pushbutton [package="[SMD]"]
  S16 = Pushbutton [package="[SMD]"]
  S17 = Pushbutton [package="[SMD]"]
  R1 = Rotary Potentiometer (Small) [maximum_resistance=100kΩ package=THT]

nets:
  N1: Part1.A0, R1.wiper
  N2: Part1.D8, S2.Pin_2, S3.Pin_2, S4.Pin_2, S5.Pin_1, S5.Pin_2
  N3: Part1.D9_PWM, S6.Pin_2, S7.Pin_2, S8.Pin_2, S9.Pin_2
  N4: Part1.D10_PWM/SS, S10.Pin_1, S10.Pin_2, S11.Pin_2, S12.Pin_2, S13.Pin_2
  N5: Part1.D11_PWM/MOSI, S14.Pin_1, S14.Pin_2, S15.Pin_2, S16.Pin_2, S17.Pin_2
  N6: Part1.D4, S2.Pin_3, S3.Pin_3, S4.Pin_3, S5.Pin_3
  N7: Part1.D5_PWM, S6.Pin_3, S6.Pin_4, S7.Pin_3, S8.Pin_3, S9.Pin_3
  N8: Part1.D6_PWM, S10.Pin_3, S10.Pin_4, S11.Pin_3, S12.Pin_3, S13.Pin_3
  N9: Part1.D7, S14.Pin_3, S15.Pin_3, S16.Pin_3, S17.Pin_3
  N10: Part1.5V, R1.leg2
  N11: Part1.GND, R1.leg1
